// Logisim project control-logic.circ as structural Verilog: 1 circuit, main circuit control_logic
module control_logic (
  input  [31:0] Instruction,
  input  BrEq,
  input  BrLt,
  output PCSel,
  output RegWEn,
  output [2:0] ImmSel,
  output BrUn,
  output ASel,
  output BSel,
  output [3:0] ALUSel,
  output MemWEn,
  output [1:0] WBSel
);

  wire and_5_out, and_8_out, and_9_out, and_15_out, and_16_out, and_17_out, and_18_out, and_19_out,
       and_20_out, and_21_out, and_22_out, and_23_out, and_24_out, and_25_out, and_26_out, comparator_1_eq,
       comparator_2_eq, comparator_3_eq, comparator_4_eq, comparator_5_eq, comparator_6_eq, comparator_7_eq,
       comparator_8_eq, comparator_9_eq, comparator_10_eq, comparator_11_eq, comparator_12_eq,
       comparator_13_eq, comparator_14_eq, comparator_15_eq, comparator_16_eq, comparator_17_eq,
       comparator_18_eq, comparator_19_eq, comparator_20_eq, comparator_21_eq, comparator_22_eq,
       comparator_23_eq, comparator_24_eq, comparator_25_eq, comparator_26_eq, comparator_27_eq,
       comparator_28_eq, comparator_29_eq, comparator_30_eq, comparator_31_eq, comparator_32_eq,
       comparator_33_eq, comparator_34_eq, comparator_35_eq, comparator_36_eq, comparator_37_eq,
       comparator_38_eq, comparator_39_eq, comparator_40_eq, comparator_41_eq, comparator_42_eq,
       comparator_43_eq, comparator_44_eq, comparator_45_eq, comparator_46_eq, comparator_47_eq,
       comparator_48_eq, comparator_49_eq, comparator_50_eq, comparator_51_eq, comparator_52_eq,
       comparator_53_eq, comparator_54_eq, comparator_55_eq, comparator_56_eq, comparator_57_eq,
       comparator_58_eq, comparator_59_eq, comparator_60_eq, comparator_61_eq, comparator_62_eq,
       comparator_63_eq, is_add, is_addi, is_and, is_andi, is_lb, is_lh, is_lw, is_mul, is_mulh, is_mulhu,
       is_or, is_ori, is_sll, is_slli, is_slt, is_slti, is_sra, is_srai, is_srl, is_srli, is_sub, is_xor,
       is_xori;
  wire [5:0] priority_encoder_1_p17;
  wire [15:14] rom_1_data;

  ROM #(.addrWidth(6), .dataWidth(16)) rom_1 (
    .addr(priority_encoder_1_p17),
    .data({rom_1_data, WBSel, MemWEn, ALUSel, BSel, ASel, BrUn, ImmSel, RegWEn}));
  Comparator #(.width(7)) comparator_1 (.a(7'b0000011), .b(Instruction[6:0]), .eq(comparator_1_eq));  // open: gt, lt
  Comparator #(.width(3)) comparator_2 (.a(3'b000), .b(Instruction[14:12]), .eq(comparator_2_eq));  // open: gt, lt
  Comparator #(.width(7)) comparator_3 (.a(7'b0000011), .b(Instruction[6:0]), .eq(comparator_3_eq));  // open: gt, lt
  Comparator #(.width(3)) comparator_4 (.a(3'b001), .b(Instruction[14:12]), .eq(comparator_4_eq));  // open: gt, lt
  Comparator #(.width(7)) comparator_5 (.a(7'b0000011), .b(Instruction[6:0]), .eq(comparator_5_eq));  // open: gt, lt
  Comparator #(.width(3)) comparator_6 (.a(3'b010), .b(Instruction[14:12]), .eq(comparator_6_eq));  // open: gt, lt
  Comparator #(.width(7)) comparator_7 (.a(7'b0010011), .b(Instruction[6:0]), .eq(comparator_7_eq));  // open: gt, lt
  Comparator #(.width(3)) comparator_8 (.a(3'b000), .b(Instruction[14:12]), .eq(comparator_8_eq));  // open: gt, lt
  Comparator #(.width(7)) comparator_9 (.a(7'b0010011), .b(Instruction[6:0]), .eq(comparator_9_eq));  // open: gt, lt
  Comparator #(.width(7)) comparator_10 (.a({7{1'b0}}), .b(Instruction[31:25]), .eq(comparator_10_eq));  // open: gt, lt
  Comparator #(.width(3)) comparator_11 (.a(3'b001), .b(Instruction[14:12]), .eq(comparator_11_eq));  // open: gt, lt
  Comparator #(.width(7)) comparator_12 (.a(7'b0010011), .b(Instruction[6:0]), .eq(comparator_12_eq));  // open: gt, lt
  Comparator #(.width(3)) comparator_13 (.a(3'b010), .b(Instruction[14:12]), .eq(comparator_13_eq));  // open: gt, lt
  Comparator #(.width(7)) comparator_14 (.a(7'b0010011), .b(Instruction[6:0]), .eq(comparator_14_eq));  // open: gt, lt
  Comparator #(.width(3)) comparator_15 (.a(3'b100), .b(Instruction[14:12]), .eq(comparator_15_eq));  // open: gt, lt
  Comparator #(.width(7)) comparator_16 (.a(7'b0010011), .b(Instruction[6:0]), .eq(comparator_16_eq));  // open: gt, lt
  Comparator #(.width(3)) comparator_17 (.a(3'b101), .b(Instruction[14:12]), .eq(comparator_17_eq));  // open: gt, lt
  Comparator #(.width(7)) comparator_18 (.a({7{1'b0}}), .b(Instruction[31:25]), .eq(comparator_18_eq));  // open: gt, lt
  Comparator #(.width(7)) comparator_19 (.a(7'b0010011), .b(Instruction[6:0]), .eq(comparator_19_eq));  // open: gt, lt
  Comparator #(.width(3)) comparator_20 (.a(3'b101), .b(Instruction[14:12]), .eq(comparator_20_eq));  // open: gt, lt
  Comparator #(.width(7)) comparator_21 (
    .a(7'b0100000), .b(Instruction[31:25]), .eq(comparator_21_eq));  // open: gt, lt
  Comparator #(.width(7)) comparator_22 (.a(7'b0010011), .b(Instruction[6:0]), .eq(comparator_22_eq));  // open: gt, lt
  Comparator #(.width(3)) comparator_23 (.a(3'b110), .b(Instruction[14:12]), .eq(comparator_23_eq));  // open: gt, lt
  Comparator #(.width(7)) comparator_24 (.a(7'b0010011), .b(Instruction[6:0]), .eq(comparator_24_eq));  // open: gt, lt
  Comparator #(.width(3)) comparator_25 (.a(3'b111), .b(Instruction[14:12]), .eq(comparator_25_eq));  // open: gt, lt
  // Priority_Encoder #(.select_enc(6)) priority_encoder_1: pin names not known; wires that end beside it: is_xor, is_srl, is_sra, is_or, is_and, is_lb, is_lh, is_lw, is_addi, is_slli, is_slti, is_xori, is_srli, is_srai, is_ori, is_andi, priority_encoder_1_p17
  and and_1 (is_lb, comparator_1_eq, comparator_2_eq);
  and and_2 (is_lh, comparator_3_eq, comparator_4_eq);
  and and_3 (is_lw, comparator_5_eq, comparator_6_eq);
  and and_4 (is_addi, comparator_7_eq, comparator_8_eq);
  and and_5 (and_5_out, comparator_9_eq, comparator_10_eq);
  and and_6 (is_slti, comparator_12_eq, comparator_13_eq);
  and and_7 (is_xori, comparator_14_eq, comparator_15_eq);
  and and_8 (and_8_out, comparator_16_eq, comparator_17_eq);
  and and_9 (and_9_out, comparator_19_eq, comparator_20_eq);
  and and_10 (is_ori, comparator_22_eq, comparator_23_eq);
  and and_11 (is_andi, comparator_24_eq, comparator_25_eq);
  and and_12 (is_srli, and_8_out, comparator_18_eq);
  and and_13 (is_srai, and_9_out, comparator_21_eq);
  and and_14 (is_slli, and_5_out, comparator_11_eq);
  Comparator #(.width(1)) comparator_26 (.a(1'b1), .b(BrEq), .eq(comparator_26_eq));  // open: gt, lt
  Comparator #(.width(1)) comparator_27 (.a(1'b1), .b(BrLt), .eq(comparator_27_eq));  // open: gt, lt
  or or_1 (PCSel, comparator_26_eq, comparator_27_eq);
  Comparator #(.width(7)) comparator_28 (.a(7'b0110011), .b(Instruction[6:0]), .eq(comparator_28_eq));  // open: gt, lt
  Comparator #(.width(3)) comparator_29 (.a(3'b000), .b(Instruction[14:12]), .eq(comparator_29_eq));  // open: gt, lt
  Comparator #(.width(7)) comparator_30 (.a({7{1'b0}}), .b(Instruction[31:25]), .eq(comparator_30_eq));  // open: gt, lt
  Comparator #(.width(7)) comparator_31 (.a(7'b0110011), .b(Instruction[6:0]), .eq(comparator_31_eq));  // open: gt, lt
  Comparator #(.width(3)) comparator_32 (.a(3'b000), .b(Instruction[14:12]), .eq(comparator_32_eq));  // open: gt, lt
  Comparator #(.width(7)) comparator_33 (
    .a(7'b0100000), .b(Instruction[31:25]), .eq(comparator_33_eq));  // open: gt, lt
  Comparator #(.width(7)) comparator_34 (.a(7'b0110011), .b(Instruction[6:0]), .eq(comparator_34_eq));  // open: gt, lt
  Comparator #(.width(3)) comparator_35 (.a(3'b111), .b(Instruction[14:12]), .eq(comparator_35_eq));  // open: gt, lt
  Comparator #(.width(7)) comparator_36 (.a({7{1'b0}}), .b(Instruction[31:25]), .eq(comparator_36_eq));  // open: gt, lt
  Comparator #(.width(7)) comparator_37 (.a(7'b0110011), .b(Instruction[6:0]), .eq(comparator_37_eq));  // open: gt, lt
  Comparator #(.width(3)) comparator_38 (.a(3'b110), .b(Instruction[14:12]), .eq(comparator_38_eq));  // open: gt, lt
  Comparator #(.width(7)) comparator_39 (.a({7{1'b0}}), .b(Instruction[31:25]), .eq(comparator_39_eq));  // open: gt, lt
  Comparator #(.width(7)) comparator_40 (.a(7'b0110011), .b(Instruction[6:0]), .eq(comparator_40_eq));  // open: gt, lt
  Comparator #(.width(3)) comparator_41 (.a(3'b100), .b(Instruction[14:12]), .eq(comparator_41_eq));  // open: gt, lt
  Comparator #(.width(7)) comparator_42 (.a({7{1'b0}}), .b(Instruction[31:25]), .eq(comparator_42_eq));  // open: gt, lt
  Comparator #(.width(7)) comparator_43 (.a(7'b0110011), .b(Instruction[6:0]), .eq(comparator_43_eq));  // open: gt, lt
  Comparator #(.width(3)) comparator_44 (.a(3'b001), .b(Instruction[14:12]), .eq(comparator_44_eq));  // open: gt, lt
  Comparator #(.width(7)) comparator_45 (.a({7{1'b0}}), .b(Instruction[31:25]), .eq(comparator_45_eq));  // open: gt, lt
  Comparator #(.width(7)) comparator_46 (.a(7'b0110011), .b(Instruction[6:0]), .eq(comparator_46_eq));  // open: gt, lt
  Comparator #(.width(3)) comparator_47 (.a(3'b101), .b(Instruction[14:12]), .eq(comparator_47_eq));  // open: gt, lt
  Comparator #(.width(7)) comparator_48 (.a({7{1'b0}}), .b(Instruction[31:25]), .eq(comparator_48_eq));  // open: gt, lt
  Comparator #(.width(7)) comparator_49 (.a(7'b0110011), .b(Instruction[6:0]), .eq(comparator_49_eq));  // open: gt, lt
  Comparator #(.width(3)) comparator_50 (.a(3'b101), .b(Instruction[14:12]), .eq(comparator_50_eq));  // open: gt, lt
  Comparator #(.width(7)) comparator_51 (
    .a(7'b0100000), .b(Instruction[31:25]), .eq(comparator_51_eq));  // open: gt, lt
  Comparator #(.width(7)) comparator_52 (.a(7'b0110011), .b(Instruction[6:0]), .eq(comparator_52_eq));  // open: gt, lt
  Comparator #(.width(3)) comparator_53 (.a(3'b010), .b(Instruction[14:12]), .eq(comparator_53_eq));  // open: gt, lt
  Comparator #(.width(7)) comparator_54 (.a({7{1'b0}}), .b(Instruction[31:25]), .eq(comparator_54_eq));  // open: gt, lt
  Comparator #(.width(7)) comparator_55 (.a(7'b0110011), .b(Instruction[6:0]), .eq(comparator_55_eq));  // open: gt, lt
  Comparator #(.width(3)) comparator_56 (.a(3'b000), .b(Instruction[14:12]), .eq(comparator_56_eq));  // open: gt, lt
  Comparator #(.width(7)) comparator_57 (
    .a(7'b0000001), .b(Instruction[31:25]), .eq(comparator_57_eq));  // open: gt, lt
  Comparator #(.width(7)) comparator_58 (.a(7'b0110011), .b(Instruction[6:0]), .eq(comparator_58_eq));  // open: gt, lt
  Comparator #(.width(3)) comparator_59 (.a(3'b001), .b(Instruction[14:12]), .eq(comparator_59_eq));  // open: gt, lt
  Comparator #(.width(7)) comparator_60 (
    .a(7'b0000001), .b(Instruction[31:25]), .eq(comparator_60_eq));  // open: gt, lt
  Comparator #(.width(7)) comparator_61 (.a(7'b0110011), .b(Instruction[6:0]), .eq(comparator_61_eq));  // open: gt, lt
  Comparator #(.width(3)) comparator_62 (.a(3'b111), .b(Instruction[14:12]), .eq(comparator_62_eq));  // open: gt, lt
  Comparator #(.width(7)) comparator_63 (
    .a(7'b0000001), .b(Instruction[31:25]), .eq(comparator_63_eq));  // open: gt, lt
  and and_15 (and_15_out, comparator_28_eq, comparator_29_eq);
  and and_16 (and_16_out, comparator_31_eq, comparator_32_eq);
  and and_17 (and_17_out, comparator_34_eq, comparator_35_eq);
  and and_18 (and_18_out, comparator_37_eq, comparator_38_eq);
  and and_19 (and_19_out, comparator_40_eq, comparator_41_eq);
  and and_20 (and_20_out, comparator_43_eq, comparator_44_eq);
  and and_21 (and_21_out, comparator_46_eq, comparator_47_eq);
  and and_22 (and_22_out, comparator_49_eq, comparator_50_eq);
  and and_23 (and_23_out, comparator_52_eq, comparator_53_eq);
  and and_24 (and_24_out, comparator_55_eq, comparator_56_eq);
  and and_25 (and_25_out, comparator_58_eq, comparator_59_eq);
  and and_26 (and_26_out, comparator_61_eq, comparator_62_eq);
  and and_27 (is_add, and_15_out, comparator_30_eq);
  and and_28 (is_sub, and_16_out, comparator_33_eq);
  and and_29 (is_and, and_17_out, comparator_36_eq);
  and and_30 (is_or, and_18_out, comparator_39_eq);
  and and_31 (is_xor, and_19_out, comparator_42_eq);
  and and_32 (is_sll, and_20_out, comparator_45_eq);
  and and_33 (is_srl, and_21_out, comparator_48_eq);
  and and_34 (is_sra, and_22_out, comparator_51_eq);
  and and_35 (is_slt, and_23_out, comparator_54_eq);
  and and_36 (is_mul, and_24_out, comparator_57_eq);
  and and_37 (is_mulh, and_25_out, comparator_60_eq);
  and and_38 (is_mulhu, and_26_out, comparator_63_eq);

  // Other names for the same wires on the sheet: opcode[6:0] = Instruction[6:0]; funct3[2:0] = Instruction[14:12];
  //   funct7[6:0] = Instruction[31:25]

  // Notes on the sheet:
  //   INPUTS to your circuit
  //   Connect ROM Input here ->
  //   contents of rom_1 (hex, n*v repeats v):
  //   100d 140d 160d 108d 148d 158d 110d 120d 128d 168d 130d 138d 2841 2841 2841 1041 10c1 1141 1241 12c1
  //   16c1 1341 13c1 3042 3042 3042 4*1064 1074 1074 1067 1047 69 4b
  //   ROM FOR CONTROL LOGIC
  //   DON'T CHANGE THE LOCATIONS OF THE INPUTS AND OUTPUTS!
  //   This is only if you choose to do the ROM option
  //   CONNECT
  //   WIRE
  //   TO
  //   USE
  //   ROM
  //   OUTPUT from your circuit
  //   Reminder: If using ROM, use combinational logic for PCSel
endmodule
