// Logisim project regfile.circ as structural Verilog: 1 circuit, main circuit regfile
module regfile (
  input  [4:0] ReadIndex1,
  input  [4:0] ReadIndex2,
  input  [4:0] WriteIndex,
  input  [31:0] WriteData,
  input  RegWEn,
  input  clk,
  output [31:0] ra,
  output [31:0] sp,
  output [31:0] t0,
  output [31:0] t1,
  output [31:0] t2,
  output [31:0] s0,
  output [31:0] s1,
  output [31:0] a0,
  output [31:0] ReadData1,
  output [31:0] ReadData2
);

  wire demultiplexer_1_out1, demultiplexer_1_out2, demultiplexer_1_out3, demultiplexer_1_out4,
       demultiplexer_1_out5, demultiplexer_1_out6, demultiplexer_1_out7, demultiplexer_1_out8,
       demultiplexer_1_out9, demultiplexer_1_out10, demultiplexer_1_out11, demultiplexer_1_out12,
       demultiplexer_1_out13, demultiplexer_1_out14, demultiplexer_1_out15, demultiplexer_1_out16,
       demultiplexer_1_out17, demultiplexer_1_out18, demultiplexer_1_out19, demultiplexer_1_out20,
       demultiplexer_1_out21, demultiplexer_1_out22, demultiplexer_1_out23, demultiplexer_1_out24,
       demultiplexer_1_out25, demultiplexer_1_out26, demultiplexer_1_out27, demultiplexer_1_out28,
       demultiplexer_1_out29, demultiplexer_1_out30, demultiplexer_1_out31;
  wire [31:0] dx0, dx3, dx4, dx11, dx12, dx13, dx14, dx15, dx16, dx17, dx18, dx19, dx20, dx21, dx22, dx23,
       dx24, dx25, dx26, dx27, dx28, dx29, dx30, dx31;

  Multiplexer #(.select(5), .width(32)) multiplexer_1 (
    .in0(dx0), .in1(ra), .in2(sp), .in3(dx3), .in4(dx4), .in5(t0), .in6(t1), .in7(t2), .in8(s0), .in9(s1),
    .in10(a0), .in11(dx11), .in12(dx12), .in13(dx13), .in14(dx14), .in15(dx15), .in16(dx16), .in17(dx17),
    .in18(dx18), .in19(dx19), .in20(dx20), .in21(dx21), .in22(dx22), .in23(dx23), .in24(dx24), .in25(dx25),
    .in26(dx26), .in27(dx27), .in28(dx28), .in29(dx29), .in30(dx30), .in31(dx31), .out(ReadData2),
    .sel(ReadIndex2));
  Multiplexer #(.select(5), .width(32)) multiplexer_2 (
    .in0(dx0), .in1(ra), .in2(sp), .in3(dx3), .in4(dx4), .in5(t0), .in6(t1), .in7(t2), .in8(s0), .in9(s1),
    .in10(a0), .in11(dx11), .in12(dx12), .in13(dx13), .in14(dx14), .in15(dx15), .in16(dx16), .in17(dx17),
    .in18(dx18), .in19(dx19), .in20(dx20), .in21(dx21), .in22(dx22), .in23(dx23), .in24(dx24), .in25(dx25),
    .in26(dx26), .in27(dx27), .in28(dx28), .in29(dx29), .in30(dx30), .in31(dx31), .out(ReadData1),
    .sel(ReadIndex1));
  Demultiplexer #(.select(5)) demultiplexer_1 (
    .out1(demultiplexer_1_out1), .out2(demultiplexer_1_out2), .out3(demultiplexer_1_out3),
    .out4(demultiplexer_1_out4), .out5(demultiplexer_1_out5), .out6(demultiplexer_1_out6),
    .out7(demultiplexer_1_out7), .out8(demultiplexer_1_out8), .out9(demultiplexer_1_out9),
    .out10(demultiplexer_1_out10), .out11(demultiplexer_1_out11), .out12(demultiplexer_1_out12),
    .out13(demultiplexer_1_out13), .out14(demultiplexer_1_out14), .out15(demultiplexer_1_out15),
    .out16(demultiplexer_1_out16), .out17(demultiplexer_1_out17), .out18(demultiplexer_1_out18),
    .out19(demultiplexer_1_out19), .out20(demultiplexer_1_out20), .out21(demultiplexer_1_out21),
    .out22(demultiplexer_1_out22), .out23(demultiplexer_1_out23), .out24(demultiplexer_1_out24),
    .out25(demultiplexer_1_out25), .out26(demultiplexer_1_out26), .out27(demultiplexer_1_out27),
    .out28(demultiplexer_1_out28), .out29(demultiplexer_1_out29), .out30(demultiplexer_1_out30),
    .out31(demultiplexer_1_out31), .in(RegWEn), .sel(WriteIndex));  // open: out0
  Register #(.width(32)) register_1 (.D(WriteData), .en(1'b0), .clk(clk), .Q(dx0));  // open: clr
  Register #(.width(32)) register_2 (.D(WriteData), .en(demultiplexer_1_out1), .clk(clk), .Q(ra));  // open: clr
  Register #(.width(32)) register_3 (.D(WriteData), .en(demultiplexer_1_out2), .clk(clk), .Q(sp));  // open: clr
  Register #(.width(32)) register_4 (.D(WriteData), .en(demultiplexer_1_out3), .clk(clk), .Q(dx3));  // open: clr
  Register #(.width(32)) register_5 (.D(WriteData), .en(demultiplexer_1_out4), .clk(clk), .Q(dx4));  // open: clr
  Register #(.width(32)) register_6 (.D(WriteData), .en(demultiplexer_1_out5), .clk(clk), .Q(t0));  // open: clr
  Register #(.width(32)) register_7 (.D(WriteData), .en(demultiplexer_1_out6), .clk(clk), .Q(t1));  // open: clr
  Register #(.width(32)) register_8 (.D(WriteData), .en(demultiplexer_1_out7), .clk(clk), .Q(t2));  // open: clr
  Register #(.width(32)) register_9 (.D(WriteData), .en(demultiplexer_1_out8), .clk(clk), .Q(s0));  // open: clr
  Register #(.width(32)) register_10 (.D(WriteData), .en(demultiplexer_1_out9), .clk(clk), .Q(s1));  // open: clr
  Register #(.width(32)) register_11 (.D(WriteData), .en(demultiplexer_1_out10), .clk(clk), .Q(a0));  // open: clr
  Register #(.width(32)) register_12 (.D(WriteData), .en(demultiplexer_1_out11), .clk(clk), .Q(dx11));  // open: clr
  Register #(.width(32)) register_13 (.D(WriteData), .en(demultiplexer_1_out12), .clk(clk), .Q(dx12));  // open: clr
  Register #(.width(32)) register_14 (.D(WriteData), .en(demultiplexer_1_out13), .clk(clk), .Q(dx13));  // open: clr
  Register #(.width(32)) register_15 (.D(WriteData), .en(demultiplexer_1_out14), .clk(clk), .Q(dx14));  // open: clr
  Register #(.width(32)) register_16 (.D(WriteData), .en(demultiplexer_1_out15), .clk(clk), .Q(dx15));  // open: clr
  Register #(.width(32)) register_17 (.D(WriteData), .en(demultiplexer_1_out16), .clk(clk), .Q(dx16));  // open: clr
  Register #(.width(32)) register_18 (.D(WriteData), .en(demultiplexer_1_out17), .clk(clk), .Q(dx17));  // open: clr
  Register #(.width(32)) register_19 (.D(WriteData), .en(demultiplexer_1_out18), .clk(clk), .Q(dx18));  // open: clr
  Register #(.width(32)) register_20 (.D(WriteData), .en(demultiplexer_1_out19), .clk(clk), .Q(dx19));  // open: clr
  Register #(.width(32)) register_21 (.D(WriteData), .en(demultiplexer_1_out20), .clk(clk), .Q(dx20));  // open: clr
  Register #(.width(32)) register_22 (.D(WriteData), .en(demultiplexer_1_out21), .clk(clk), .Q(dx21));  // open: clr
  Register #(.width(32)) register_23 (.D(WriteData), .en(demultiplexer_1_out22), .clk(clk), .Q(dx22));  // open: clr
  Register #(.width(32)) register_24 (.D(WriteData), .en(demultiplexer_1_out23), .clk(clk), .Q(dx23));  // open: clr
  Register #(.width(32)) register_25 (.D(WriteData), .en(demultiplexer_1_out24), .clk(clk), .Q(dx24));  // open: clr
  Register #(.width(32)) register_26 (.D(WriteData), .en(demultiplexer_1_out25), .clk(clk), .Q(dx25));  // open: clr
  Register #(.width(32)) register_27 (.D(WriteData), .en(demultiplexer_1_out26), .clk(clk), .Q(dx26));  // open: clr
  Register #(.width(32)) register_28 (.D(WriteData), .en(demultiplexer_1_out27), .clk(clk), .Q(dx27));  // open: clr
  Register #(.width(32)) register_29 (.D(WriteData), .en(demultiplexer_1_out28), .clk(clk), .Q(dx28));  // open: clr
  Register #(.width(32)) register_30 (.D(WriteData), .en(demultiplexer_1_out29), .clk(clk), .Q(dx29));  // open: clr
  Register #(.width(32)) register_31 (.D(WriteData), .en(demultiplexer_1_out30), .clk(clk), .Q(dx30));  // open: clr
  Register #(.width(32)) register_32 (.D(WriteData), .en(demultiplexer_1_out31), .clk(clk), .Q(dx31));  // open: clr

  // Other names for the same wires on the sheet: dx1[31:0] = ra; dx2[31:0] = sp; dx5[31:0] = t0; dx6[31:0] = t1;
  //   dx7[31:0] = t2; dx8[31:0] = s0; dx9[31:0] = s1; dx10[31:0] = a0

  // Notes on the sheet:
  //   INPUTS to your circuit
  //   DON'T CHANGE THE LOCATIONS OF THE INPUTS AND OUTPUTS!
  //   These are DEBUG/TEST outputs from your circuit.
  //   OUTPUTS from your circuit
endmodule
